# Fritzing sketch photon (saved by Fritzing 0.9.3b)
breadboards: 1

parts:
  M1 = Stepper Motor - Bipolar  # not connected
  Power_plug1 = Power plug  # not connected
  Part1 = Arduino Uno (Rev3)
  LED1 = LED - 3mm [color="White (6500K)" package="3 mm [THT]"]
  R1 = Resistor [tolerance=±5% resistance=220 package=THT]
  R2 = PHOTOCELL [package=photocell-kit]  # not connected
  VCC1 = Battery block 9V  # not connected

nets:
  N1: Part1.3V3, LED1.cathode
  N2: Part1.GND, R1.Pin_1
  N3: LED1.anode, R1.Pin_0

notes:
  Photoresistor
  Vcc to 3.3 V
  Ground to Ground
  Analog Signal to A0
  9 V battery regulated to the 5 V. We are only using this power source for the stepper motor.
  Stepper motor driver
  The cable from the motor fits into this
  + to 5 V
  - to GND
  4 command inputs in order
  Pin 9
  Pin 10
  Pin 11
  Pin 12
  They must not be switched out of order sequentially
